// Logisim project traffic light peoject FINAL.circ as structural Verilog: 1 circuit, main circuit main
module main (
  input  in_1,
  input  in_2
);

  wire and_1_out, and_2_out, and_3_out, and_4_out, and_5_out, and_6_out, and_7_out, and_8_out, and_9_out,
       and_10_out, and_11_out, and_12_out, not_1_out, not_2_out, not_3_out, not_4_out, not_5_out, not_6_out,
       or_1_out, or_2_out, or_3_out, or_4_out, or_5_out, or_6_out, or_7_out, or_8_out, or_9_out;

  not not_1 (not_1_out, in_1);
  not not_2 (not_2_out, in_2);
  and and_1 (and_1_out, not_1_out, not_2_out);
  and and_2 (and_2_out, in_1, in_1, not_2_out);
  and and_3 (and_3_out, in_2, in_2, not_1_out);
  and and_4 (and_4_out, in_2, in_1);
  not not_3 (not_3_out, in_1);
  not not_4 (not_4_out, in_2);
  or or_1 (or_1_out, and_4_out, and_2_out);
  or or_2 (or_2_out, and_1_out, and_2_out, and_3_out);
  LED led_1 (.in(or_2_out));
  LED led_2 (.in(and_4_out));
  not not_5 (not_5_out, in_1);
  LED led_3 (.in(or_1_out));
  LED led_4 (.in(and_3_out));
  LED led_5 (.in(and_1_out));
  not not_6 (not_6_out, in_2);
  or or_3 (or_3_out, or_1_out, and_3_out);
  and and_5 (and_5_out, not_3_out, not_4_out);
  and and_6 (and_6_out, in_1, in_1, not_4_out);
  and and_7 (and_7_out, in_2, in_2, not_3_out);
  and and_8 (and_8_out, in_2, in_1);
  or or_4 (or_4_out, and_9_out, or_8_out, or_8_out, or_8_out);
  and and_9 (and_9_out, not_5_out, not_6_out);
  and and_10 (and_10_out, in_1, in_1, not_6_out);
  and and_11 (and_11_out, in_2, in_2, not_5_out);
  and and_12 (and_12_out, in_2, in_1);
  LED led_6 (.in(and_8_out));
  LED led_7 (.in(and_10_out));
  LED led_8 (.in(or_4_out));
  LED led_9 (.in(or_8_out));
  or or_5 (or_5_out, and_5_out, and_8_out);
  or or_6 (or_6_out, and_5_out, and_6_out, and_7_out);
  LED led_10 (.in(or_6_out));
  or or_7 (or_7_out, or_5_out, or_5_out, and_6_out);
  LED led_11 (.in(and_9_out));
  or or_8 (or_8_out, and_11_out, and_12_out, and_11_out);
  LED led_12 (.in(and_7_out));
  LED led_13 (.in(or_5_out));
  LED led_14 (.in(and_6_out));
  LED led_15 (.in(and_1_out));
  LED led_16 (.in(and_7_out));
  LED led_17 (.in(or_7_out));
  LED led_18 (.in(and_10_out));
  LED led_19 (.in(or_3_out));
  LED led_20 (.in(and_12_out));
  LED led_21 (.in(or_9_out));
  or or_9 (or_9_out, and_9_out, and_10_out, and_11_out, and_11_out);
endmodule
